// Logisim project 000.Dado_LED_Logico.circ as structural Verilog: 6 circuits, main circuit main
module main (
  input  A2,
  input  A1,
  input  A0,
  output L1,
  output L2,
  output L3,
  output L4,
  output L5,
  output L6,
  output L7
);

  DADO dado_1 (.A2(A2), .A1(A1), .A0(A0), .L1(L1), .L3(L3), .L6(L6), .L4(L4), .L2(L2), .L5(L5), .L7(L7));
endmodule

module L1_e_L7 (
  input  A1,
  input  A2,
  output out_3
);

  or or_1 (out_3, A1, A2);
endmodule

module L2_e_L6 (
  input  A2,
  output out_2
);


  assign out_2 = A2;
endmodule

module L3_e_L5 (
  input  A1,
  input  A2,
  output out_3
);

  and and_1 (out_3, A1, A2);
endmodule

module L4 (
  input  A0,
  output out_2
);


  assign out_2 = A0;
endmodule

module DADO (
  input  A2,
  input  A1,
  input  A0,
  output L1,
  output L2,
  output L3,
  output L4,
  output L5,
  output L6,
  output L7
);

  or X (L1, A1, A2);
  and Y (L3, A1, A2);

  assign L2 = A2;
  assign L4 = A0;
  assign L5 = L3;
  assign L6 = A2;
  assign L7 = L1;

  // Notes on the sheet:
  //   A
  //   B
  //   C
endmodule
