// Logisim project 001.Alarme_Bancario.circ as structural Verilog
module Sistema_de_Alarme_Bancario (
  input  P,
  input  V,
  input  C,
  input  E,
  output S
);

  wire and_1_out, and_2_out;

  and and_1 (and_1_out, P, E, ~V);  // AND_Gate
  and and_2 (and_2_out, P, C, ~V);  // AND_Gate
  or or_1 (S, and_1_out, and_2_out);
endmodule
