// Logisim project 002.Sistema_de_Voto.circ as structural Verilog: 4 circuits, main circuit main
module main (
  input  X,
  input  Y,
  input  Z,
  input  W,
  output APROVADO,
  output REPROVADO,
  output EMPATE
);

  Aprovado aprovado_1 (.X(X), .Y(Y), .Z(Z), .W(W), .A(APROVADO));
  Reprovado reprovado_1 (.R(REPROVADO), .X(X), .Y(Y), .Z(Z), .W(W));
  Empate empate_1 (.X(X), .Y(Y), .Z(Z), .W(W), .E(EMPATE));
endmodule

module Aprovado (
  input  X,
  input  Y,
  input  Z,
  input  W,
  output A
);

  wire and_1_out, and_2_out, and_3_out, and_4_out;

  and and_1 (and_1_out, Y, Z, W);
  and and_2 (and_2_out, X, Z, W);
  and and_3 (and_3_out, X, Y, W);
  and and_4 (and_4_out, X, Y, Z);
  or or_1 (A, and_1_out, and_2_out, and_3_out, and_4_out);
endmodule

module Reprovado (
  input  X,
  input  Y,
  input  Z,
  input  W,
  output R
);

  wire and_1_out, and_2_out, and_3_out, and_4_out;

  and and_1 (and_1_out, ~X, ~Z, ~W);  // AND_Gate
  and and_2 (and_2_out, ~X, ~Y, ~Z);  // AND_Gate
  and and_3 (and_3_out, ~Y, ~Z, ~W);  // AND_Gate
  and and_4 (and_4_out, ~X, ~Y, ~W);  // AND_Gate
  or or_1 (R, and_1_out, and_2_out, and_3_out, and_4_out);
endmodule

module Empate (
  input  X,
  input  Y,
  input  Z,
  input  W,
  output E
);

  wire and_1_out, and_2_out, and_3_out, and_4_out, and_5_out, and_6_out;

  and and_1 (and_1_out, ~X, ~Y, Z, W);  // AND_Gate
  and and_2 (and_2_out, ~X, Y, ~Z, W);  // AND_Gate
  and and_3 (and_3_out, ~X, Y, Z, ~W);  // AND_Gate
  and and_4 (and_4_out, X, Y, ~Z, ~W);  // AND_Gate
  and and_5 (and_5_out, X, ~Y, ~Z, W);  // AND_Gate
  and and_6 (and_6_out, X, ~Y, Z, ~W);  // AND_Gate
  or or_1 (E, and_1_out, and_2_out, and_3_out, and_4_out, and_5_out, and_6_out);
endmodule
