// Logisim project 003.Maquina_Com_Prioridade.circ as structural Verilog
module MAQUINA (
  input  A,
  input  B,
  input  C,
  input  D,
  output S1,
  output S2,
  output S3,
  output S4
);

  wire and_1_out, and_2_out, and_3_out, and_4_out, and_5_out;

  and and_1 (and_1_out, ~A, C);  // AND_Gate
  and and_2 (and_2_out, ~B, C);  // AND_Gate
  and and_3 (and_3_out, ~A, ~B, D);  // AND_Gate
  and and_4 (and_4_out, ~A, ~C, D);  // AND_Gate
  and and_5 (and_5_out, ~B, ~C, D);  // AND_Gate
  or or_1 (S3, and_1_out, and_2_out);
  or or_2 (S4, and_3_out, and_4_out, and_5_out);

  assign S1 = A;
  assign S2 = B;
endmodule
