// Logisim project 004.Sensor_de_Perigo_Quimico.circ as structural Verilog
module Sensor_de_Perigo_Quimico (
  input  A,
  input  B,
  input  C,
  input  D,
  output P
);

  wire and_1_out, and_2_out;

  and and_1 (and_1_out, ~A, C, D);  // AND_Gate
  or or_1 (P, and_1_out, and_2_out);
  and and_2 (and_2_out, ~A, B, C);  // AND_Gate
endmodule
