// Logisim project 005.Sensor_de_Perigo_FLCA.circ as structural Verilog: 1 circuit, main circuit main
module main (
  input  F,
  input  L,
  input  C,
  input  A,
  output B
);

  wire and_1_out, and_2_out, and_3_out, and_4_out;

  and and_1 (and_1_out, ~F, C, A);  // AND_Gate
  and and_2 (and_2_out, ~F, C, L);  // AND_Gate
  and and_3 (and_3_out, F, ~C, ~A);  // AND_Gate
  and and_4 (and_4_out, F, ~C, ~L);  // AND_Gate
  or or_1 (B, and_1_out, and_2_out, and_3_out, and_4_out);
endmodule
