// Logisim project 006.Sensor_de_Alerta_de_Tanque.circ as structural Verilog: 1 circuit, main circuit main
module main (
  input  t,
  input  p,
  input  n,
  input  f,
  output S
);

  wire and_1_out, and_2_out, and_3_out;

  and and_1 (and_1_out, p, ~n);  // AND_Gate
  and and_2 (and_2_out, t, ~n);  // AND_Gate
  and and_3 (and_3_out, t, p);
  or or_1 (S, and_1_out, and_2_out, and_3_out);
endmodule
