// Logisim project 007.Diplay_Incompleto.circ as structural Verilog
module a (
  input  x,
  input  y,
  input  z,
  input  w,
  output out_5
);

  wire and_1_out, and_2_out, and_3_out, and_4_out, and_5_out;

  and and_1 (and_1_out, z, ~w);  // AND_Gate
  and and_2 (and_2_out, ~x, z);  // AND_Gate
  and and_3 (and_3_out, y, z);
  and and_4 (and_4_out, x, ~w);  // AND_Gate
  and and_5 (and_5_out, ~y, ~z, ~w);  // AND_Gate
  or or_1 (out_5, and_1_out, and_2_out, and_3_out, and_4_out, and_5_out);
endmodule

module b (
  input  x,
  input  y,
  input  z,
  input  w,
  output out_5
);

  wire and_1_out, and_2_out, and_3_out, and_4_out, and_5_out;

  and and_1 (and_1_out, ~x, ~y);  // AND_Gate
  and and_2 (and_2_out, ~y, ~z);  // AND_Gate
  and and_3 (and_3_out, ~x, ~z, ~w);  // AND_Gate
  and and_4 (and_4_out, ~x, z, w);  // AND_Gate
  and and_5 (and_5_out, ~y, z, ~w);  // AND_Gate
  or or_1 (out_5, and_1_out, and_2_out, and_3_out, and_4_out, and_5_out);
endmodule

module c (
  input  x,
  input  y,
  input  z,
  input  w,
  output out_5
);

  wire and_1_out, and_2_out, and_3_out, and_4_out;

  and and_1 (and_1_out, ~x, ~z);  // AND_Gate
  and and_2 (and_2_out, ~x, w);  // AND_Gate
  and and_3 (and_3_out, x, ~y);  // AND_Gate
  and and_4 (and_4_out, ~x, y, z);  // AND_Gate
  or or_1 (out_5, and_1_out, and_2_out, and_3_out, and_4_out);
endmodule

module d (
  input  x,
  input  y,
  input  z,
  input  w,
  output out_5
);

  wire and_1_out, and_2_out, and_3_out, and_4_out, and_5_out;

  and and_1 (and_1_out, x, ~z);  // AND_Gate
  and and_2 (and_2_out, y, ~z, w);  // AND_Gate
  and and_3 (and_3_out, ~y, z, w);  // AND_Gate
  and and_4 (and_4_out, ~x, ~y, ~w);  // AND_Gate
  and and_5 (and_5_out, y, z, ~w);  // AND_Gate
  or or_1 (out_5, and_1_out, and_2_out, and_3_out, and_4_out, and_5_out);
endmodule

module e (
  input  x,
  input  y,
  input  z,
  input  w,
  output out_5
);

  wire and_1_out, and_2_out, and_3_out, and_4_out;

  and and_1 (and_1_out, ~z, w);  // AND_Gate
  and and_2 (and_2_out, x, y);
  and and_3 (and_3_out, x, ~y, z);  // AND_Gate
  and and_4 (and_4_out, ~y, ~z, ~w);  // AND_Gate
  or or_1 (out_5, and_1_out, and_2_out, and_3_out, and_4_out);
endmodule

module f (
  input  x,
  input  y,
  input  z,
  input  w,
  output out_5
);

  wire and_1_out, and_2_out, and_3_out, and_4_out, and_5_out;

  and and_1 (and_1_out, ~z, ~w);  // AND_Gate
  and and_2 (and_2_out, x, ~y);  // AND_Gate
  and and_3 (and_3_out, y, ~w);  // AND_Gate
  and and_4 (and_4_out, ~x, y, ~z);  // AND_Gate
  and and_5 (and_5_out, x, y, z);
  or or_1 (out_5, and_1_out, and_2_out, and_3_out, and_4_out, and_5_out);
endmodule

module g (
  input  x,
  input  y,
  input  z,
  input  w,
  output out_5
);

  wire and_1_out, and_2_out, and_3_out, and_4_out, and_5_out;

  and and_1 (and_1_out, x, ~y);  // AND_Gate
  and and_2 (and_2_out, z, ~w);  // AND_Gate
  and and_3 (and_3_out, x, w);
  and and_4 (and_4_out, ~x, y, ~z);  // AND_Gate
  and and_5 (and_5_out, ~x, ~y, z);  // AND_Gate
  or or_1 (out_5, and_1_out, and_2_out, and_3_out, and_4_out, and_5_out);
endmodule

module display (
  input  x,
  input  y,
  input  z,
  input  w
);

  wire a_1_out_5, b_1_out_5, c_1_out_5, d_1_out_5, e_1_out_5, f_1_out_5, g_1_out_5;

  a a_1 (.x(x), .y(y), .z(z), .w(w), .out_5(a_1_out_5));
  b b_1 (.x(x), .y(y), .z(z), .w(w), .out_5(b_1_out_5));
  c c_1 (.x(x), .y(y), .z(z), .w(w), .out_5(c_1_out_5));
  d d_1 (.x(x), .y(y), .z(z), .w(w), .out_5(d_1_out_5));
  e e_1 (.x(x), .y(y), .z(z), .w(w), .out_5(e_1_out_5));
  f f_1 (.x(x), .y(y), .z(z), .w(w), .out_5(f_1_out_5));
  g g_1 (.x(x), .y(y), .z(z), .w(w), .out_5(g_1_out_5));
  _7_Segment_Display u_7_segment_display_1 (
    .g(g_1_out_5), .f(f_1_out_5), .a(a_1_out_5), .b(b_1_out_5), .e(e_1_out_5), .d(d_1_out_5), .c(c_1_out_5));  // open: dp
endmodule
