// Logisim project 008.Universilidade_da_Porta_NAND.circ as structural Verilog
module NOT (
  input  in_1,
  output out_2
);

  nand nand_1 (out_2, in_1, in_1);
endmodule

module AND (
  input  A,
  input  B,
  output C
);

  wire nand_1_out;

  nand nand_1 (nand_1_out, A, B);
  nand nand_2 (C, nand_1_out, nand_1_out);
endmodule

module OR (
  input  A,
  input  B,
  output out_3
);

  wire nand_1_out, nand_2_out;

  nand nand_1 (nand_1_out, A, A);
  nand nand_2 (nand_2_out, B, B);
  nand nand_3 (out_3, nand_1_out, nand_2_out);
endmodule
