// Logisim project 009.Universilidade_da_Porta_NOR.circ as structural Verilog
module NOT (
  input  in_1,
  output out_2
);

  nor nor_1 (out_2, in_1, in_1);
endmodule

module AND (
  input  A,
  input  B,
  output out_3
);

  wire nor_1_out;

  nor nor_1 (nor_1_out, A, B);
  nor nor_2 (out_3, nor_1_out, nor_1_out);
endmodule

module OR (
  input  A,
  input  B,
  output out_3
);

  wire nor_1_out, nor_2_out;

  nor nor_1 (nor_1_out, A, A);
  nor nor_2 (nor_2_out, B, B);
  nor nor_3 (out_3, nor_1_out, nor_2_out);
endmodule
