// Logisim project 010.Classe_Somadores.circ as structural Verilog: 5 circuits, main circuit main
module main (
  input  A3,
  input  A2,
  input  A1,
  input  A0,
  input  B3,
  input  B2,
  input  B1,
  input  B0,
  input  Ci,
  output Cout,
  output S3,
  output S2,
  output S1,
  output S0
);

  adder4b adder4b_1 (
    .Cout(Cout), .Ci(Ci), .A3(A3), .A2(A2), .A1(A1), .A0(A0), .B3(B3), .B2(B2), .B1(B1), .B0(B0), .S3(S3),
    .S2(S2), .S1(S1), .S0(S0));
endmodule

module halfadder (
  input  A,
  input  B,
  output Cout,
  output S
);

  xor xor_1 (S, A, B);
  and and_1 (Cout, A, B);
endmodule

module fulladder (
  input  A,
  input  B,
  input  Cin,
  output Cout,
  output S
);

  wire and_1_out, and_2_out, and_3_out;

  and and_1 (and_1_out, A, B);
  and and_2 (and_2_out, B, Cin);
  and and_3 (and_3_out, A, Cin);
  or or_1 (Cout, and_1_out, and_2_out, and_3_out);
  ExactlyOne xor_1 (.out(S), .in0(A), .in1(B), .in2(Cin));
endmodule

module adder4b (
  input  A3,
  input  A2,
  input  A1,
  input  A0,
  input  B3,
  input  B2,
  input  B1,
  input  B0,
  input  Ci,
  output Cout,
  output S3,
  output S2,
  output S1,
  output S0
);

  wire fulladder_2_cout, fulladder_3_cout, fulladder_4_cout;

  fulladder fulladder_1 (.A(A3), .B(B3), .Cin(fulladder_2_cout), .Cout(Cout), .S(S3));
  fulladder fulladder_2 (.A(A2), .B(B2), .Cin(fulladder_3_cout), .Cout(fulladder_2_cout), .S(S2));
  fulladder fulladder_3 (.A(A1), .B(B1), .Cin(fulladder_4_cout), .Cout(fulladder_3_cout), .S(S1));
  fulladder fulladder_4 (.A(A0), .B(B0), .Cin(Ci), .Cout(fulladder_4_cout), .S(S0));
endmodule

module adder8b (
  input  A3,
  input  A2,
  input  A1,
  input  A0,
  input  B3,
  input  B2,
  input  B1,
  input  B0,
  input  A3_2,
  input  A2_2,
  input  A1_2,
  input  A0_2,
  input  B3_2,
  input  B2_2,
  input  B1_2,
  input  B0_2,
  input  Ci,
  output Cout,
  output S3,
  output S2,
  output S1,
  output S0,
  output S3_2,
  output S2_2,
  output S1_2,
  output S0_2
);

  wire adder4b_2_cout;

  adder4b adder4b_1 (
    .Cout(Cout), .Ci(adder4b_2_cout), .A3(A3), .A2(A2), .A1(A1), .A0(A0), .B3(B3), .B2(B2), .B1(B1), .B0(B0),
    .S3(S3), .S2(S2), .S1(S1), .S0(S0));
  adder4b adder4b_2 (
    .Cout(adder4b_2_cout), .Ci(Ci), .A3(A3_2), .A2(A2_2), .A1(A1_2), .A0(A0_2), .B3(B3_2), .B2(B2_2),
    .B1(B1_2), .B0(B0_2), .S3(S3_2), .S2(S2_2), .S1(S1_2), .S0(S0_2));
endmodule
