// Logisim project 011.Classe_Subtratores.circ as structural Verilog: 3 circuits, main circuit main
module main (
  input  in_1,
  input  in_2,
  input  in_3,
  input  in_4,
  input  in_5,
  output out_6,
  output out_7,
  output out_8
);

  wire fullsub_ripple_borrow_2_cout;

  fullsub_ripple_borrow fullsub_ripple_borrow_1 (
    .A(in_1), .B(in_3), .Cin(fullsub_ripple_borrow_2_cout), .Cout(out_6), .S(out_7));
  fullsub_ripple_borrow fullsub_ripple_borrow_2 (
    .A(in_2), .B(in_4), .Cin(in_5), .Cout(fullsub_ripple_borrow_2_cout), .S(out_8));
endmodule

module halfsub (
  input  A,
  input  B,
  output Cout,
  output out_4
);

  and and_1 (Cout, ~A, B);  // AND_Gate
  xor xor_1 (out_4, A, B);
endmodule

module fullsub_ripple_borrow (
  input  A,
  input  B,
  input  Cin,
  output Cout,
  output S
);

  wire and_1_out, and_2_out, and_3_out;

  and and_1 (and_1_out, ~A, B);  // AND_Gate
  and and_2 (and_2_out, A, Cin);
  or or_1 (Cout, and_1_out, and_2_out, and_3_out);
  and and_3 (and_3_out, A, Cin);
  ExactlyOne xor_1 (.out(S), .in0(A), .in1(B), .in2(Cin));
endmodule
