// Logisim project 012.Classe_SubAdd.circ as structural Verilog
module fulladder (
  input  A,
  input  B,
  input  Cin,
  output Cout,
  output S
);

  wire and_1_out, and_2_out, and_3_out;

  and and_1 (and_1_out, A, B);
  and and_2 (and_2_out, A, Cin);
  and and_3 (and_3_out, B, Cin);
  or or_1 (Cout, and_1_out, and_3_out, and_2_out);
  ExactlyOne xor_1 (.out(S), .in0(A), .in1(B), .in2(Cin));
endmodule

module sub_add (
  input  A3,
  input  A2,
  input  A1,
  input  A0,
  input  B3,
  input  B2,
  input  B1,
  input  B0,
  input  Sub_Add,
  output Cout,
  output S3,
  output S2,
  output S1,
  output S0
);

  wire fulladder_2_cout, fulladder_3_cout, fulladder_4_cout, xor_1_out, xor_2_out, xor_3_out, xor_4_out;

  fulladder fulladder_1 (.A(A3), .B(xor_1_out), .Cin(fulladder_2_cout), .Cout(Cout), .S(S3));
  fulladder fulladder_2 (.A(A2), .B(xor_2_out), .Cin(fulladder_3_cout), .Cout(fulladder_2_cout), .S(S2));
  xor xor_1 (xor_1_out, B3, Sub_Add);
  fulladder fulladder_3 (.A(A1), .B(xor_3_out), .Cin(fulladder_4_cout), .Cout(fulladder_3_cout), .S(S1));
  xor xor_2 (xor_2_out, B2, Sub_Add);
  xor xor_3 (xor_3_out, B1, Sub_Add);
  fulladder fulladder_4 (.A(A0), .B(xor_4_out), .Cin(Sub_Add), .Cout(fulladder_4_cout), .S(S0));
  xor xor_4 (xor_4_out, B0, Sub_Add);
endmodule
