// Logisim project 013.Classe_Comparador_de_Magnitude.circ as structural Verilog
module comparador_de_magnitude (
  input  A0,
  input  B0,
  input  A1,
  input  A2,
  input  B1,
  input  A3,
  input  B2,
  input  B2_2,
  output A____B,
  output A___B,
  output A___B_2
);

  wire and_1_out, and_2_out, and_3_out, and_4_out, or_2_out, xnor_1_out, xnor_2_out, xnor_3_out, xnor_4_out;

  xnor xnor_1 (xnor_1_out, A0, B0);
  xnor xnor_2 (xnor_2_out, A1, B1);
  xnor xnor_3 (xnor_3_out, A2, B2);
  xnor xnor_4 (xnor_4_out, A3, B2_2);
  and and_1 (and_1_out, A0, ~B0);  // AND_Gate
  and and_2 (and_2_out, xnor_1_out, A1, ~B1);  // AND_Gate
  and and_3 (and_3_out, xnor_1_out, xnor_2_out, A2, ~B2);  // AND_Gate
  and and_4 (and_4_out, xnor_3_out, xnor_2_out, xnor_1_out, A3, ~B2_2);  // AND_Gate
  and and_5 (A____B, xnor_1_out, xnor_2_out, xnor_3_out, xnor_4_out);
  or or_1 (A___B, and_1_out, and_2_out, and_3_out, and_4_out);
  not not_1 (A___B_2, or_2_out);
  or or_2 (or_2_out, A____B, A___B);
endmodule
